// Logisim project SequentialMultiplier.circ as structural Verilog: 1 circuit, main circuit Multiplier
module Multiplier (
  input  [7:0] A,
  input  [7:0] B,
  input  START,
  output [15:0] PRODUCT,
  output DONE
);

  wire clock_1_out, not_1_out, not_2_out;
  wire [2:0] counter_1_q;
  wire [7:0] shift_register_2_q7;
  wire [15:0] adder_1_out, and_1_out, shift_register_1_q0;

  Clock clock_1 (.out(clock_1_out));
  // Probe on A
  not not_1 (not_1_out, START);
  Shift_Register #(.length(16)) shift_register_1 (
    .shift(not_1_out), .in(1'b0), .clk(clock_1_out), .load(START), .clr(1'b0), .d0(A[0]),
    .q0(shift_register_1_q0[0]), .d1(A[1]), .q1(shift_register_1_q0[1]), .d2(A[2]),
    .q2(shift_register_1_q0[2]), .d3(A[3]), .q3(shift_register_1_q0[3]), .d4(A[4]),
    .q4(shift_register_1_q0[4]), .d5(A[5]), .q5(shift_register_1_q0[5]), .d6(A[6]),
    .q6(shift_register_1_q0[6]), .d7(A[7]), .q7(shift_register_1_q0[7]), .d8(1'b0),
    .q8(shift_register_1_q0[8]), .d9(1'b0), .q9(shift_register_1_q0[9]), .d10(1'b0),
    .q10(shift_register_1_q0[10]), .d11(1'b0), .q11(shift_register_1_q0[11]), .d12(1'b0),
    .q12(shift_register_1_q0[12]), .d13(1'b0), .q13(shift_register_1_q0[13]), .d14(1'b0),
    .q14(shift_register_1_q0[14]), .d15(1'b0), .q15(shift_register_1_q0[15]));  // open: out
  assign and_1_out = shift_register_1_q0 & {16{shift_register_2_q7[0]}};  // AND_Gate and_1, 16 bits wide
  Adder #(.width(16)) adder_1 (.a(and_1_out), .b(PRODUCT), .out(adder_1_out));  // open: cin, cout
  Counter #(.width(4), .max('h8), .ongoal("stay")) counter_1 (
    .D(4'b0000), .count(1'b1), .Q({DONE, counter_1_q}), .clk(clock_1_out), .clr(START));  // open: load, carry
  // Probe on PRODUCT
  Register #(.width(16)) register_1 (.D(adder_1_out), .en(1'b1), .Q(PRODUCT), .clk(clock_1_out), .clr(START));
  // Probe on {DONE, counter_1_q}
  // Probe on B
  not not_2 (not_2_out, START);
  Shift_Register shift_register_2 (
    .shift(not_2_out), .in(1'b0), .clk(clock_1_out), .load(START), .d0(B[7]), .q0(shift_register_2_q7[7]),
    .d1(B[6]), .q1(shift_register_2_q7[6]), .d2(B[5]), .q2(shift_register_2_q7[5]), .d3(B[4]),
    .q3(shift_register_2_q7[4]), .d4(B[3]), .q4(shift_register_2_q7[3]), .d5(B[2]),
    .q5(shift_register_2_q7[2]), .d6(B[1]), .q6(shift_register_2_q7[1]), .d7(B[0]),
    .q7(shift_register_2_q7[0]));  // open: out, clr

  // Notes on the sheet:
  //   multiplicand
  //   Jonathan Bernard BLOCH, 260632216
  //   16-bit left shift register (in reverse order)
  //   accumulator for product
  //   Counter for DONE
  //   Lower 1-bit-mask
  //   multiplier
  //   8-bit right shift register
endmodule
